// Logisim project gates_circuits.circ as structural Verilog: 4 circuits, main circuit main
module main (
  input  [3:0] in_1,
  input  [3:0] in_2,
  output out_3
);

  wire xor_74ls86_1_out_9, xor_74ls86_1_out_10;

  XOR_74LS86 xor_74ls86_1 (
    .in_1(in_1[0]), .in_3(in_2[0]), .out_9(xor_74ls86_1_out_9), .out_10(xor_74ls86_1_out_10));  // open: in_5, in_7, in_6, in_8, in_2, in_4, out_11, out_12
  XOR_74LS86 xor_74ls86_2 ();  // open: in_5, in_7, in_1, in_3, in_6, in_8, in_2, in_4, out_11, out_9, out_12, out_10
  AND_74LS08 and_74ls08_1 (
    .in_1(in_1[0]), .in_3(in_2[0]), .in_2(xor_74ls86_1_out_9));  // open: in_5, in_7, in_4, in_6, in_8, out_9, out_11, out_10, out_12
  AND_74LS08 and_74ls08_2 ();  // open: in_1, in_3, in_5, in_7, in_2, in_4, in_6, in_8, out_9, out_11, out_10, out_12
  OR_74LS32 or_74ls32_1 ();  // open: in_1, in_3, in_5, in_7, in_2, in_4, in_6, in_8, out_9, out_11, out_10, out_12

  // Notes on the sheet:
  //   A
  //   B
endmodule

module XOR_74LS86 (
  input  in_1,
  input  in_2,
  input  in_3,
  input  in_4,
  input  in_5,
  input  in_6,
  input  in_7,
  input  in_8,
  output out_9,
  output out_10,
  output out_11,
  output out_12
);

  xor xor_1 (out_9, in_1, in_3);
  xor xor_2 (out_11, in_5, in_7);
  xor xor_3 (out_10, in_2, in_4);
  xor xor_4 (out_12, in_6, in_8);
endmodule

module AND_74LS08 (
  input  in_1,
  input  in_2,
  input  in_3,
  input  in_4,
  input  in_5,
  input  in_6,
  input  in_7,
  input  in_8,
  output out_9,
  output out_10,
  output out_11,
  output out_12
);

  and and_1 (out_9, in_1, in_3);
  and and_2 (out_11, in_5, in_7);
  and and_3 (out_10, in_2, in_4);
  and and_4 (out_12, in_6, in_8);
endmodule

module OR_74LS32 (
  input  in_1,
  input  in_2,
  input  in_3,
  input  in_4,
  input  in_5,
  input  in_6,
  input  in_7,
  input  in_8,
  output out_9,
  output out_10,
  output out_11,
  output out_12
);

  or or_1 (out_9, in_1, in_3);
  or or_2 (out_11, in_5, in_7);
  or or_3 (out_10, in_2, in_4);
  or or_4 (out_12, in_6, in_8);
endmodule
